// Logisim project home work 10.circ as structural Verilog: 1 circuit, main circuit main
module main (
  input  Enable,
  input  Fill,
  output Out4,
  output Out3
);

  wire and_1_out, CLK_out, j_k_ff_1_qn;

  Clock CLK (.out(CLK_out));
  J_K_Flip_Flop j_k_ff_1 (.J(Enable), .clk(CLK_out), .K(Fill), .Q(Out4), .Qn(j_k_ff_1_qn));  // open: preset, en, reset
  and and_1 (and_1_out, Enable, Out4);
  J_K_Flip_Flop j_k_ff_2 (.J(and_1_out), .clk(CLK_out), .K(j_k_ff_1_qn), .Q(Out3));  // open: Qn, preset, en, reset

  // Notes on the sheet:
  //   Right Shift Register
  //   Change state on PGT of CLK
endmodule
